# Fritzing sketch FootSwitch3 (saved by Fritzing 0.9.3b)
stripboards: 1

parts:
  Ch3_LED = LED - 5mm [color="Red (633nm)" package="5 mm [THT]"]
  Solo_LED = LED - 5mm [color="Red (633nm)" package="5 mm [THT]"]
  Ch1_Switch = Toggle Switch [package=THT]
  Ch2_Switch = Toggle Switch [package=THT]
  Ch3_Switch = Toggle Switch [package=THT]
  Solo_Switch = Toggle Switch [package=THT]
  Amp1_LED = LED - 5mm [color="Orange (612nm)" package="5 mm [THT]"]
  Ch2_LED = LED - 5mm [color="Orange (620nm)" package="5 mm [THT]"]
  Ch1_LED = LED - 5mm [color="Blue (525nm)" package="5 mm [THT]"]
  Amp_Switch = SWITCH-DPDT [package=gpi-152-3013]
  Amp2_LED = LED - 5mm [color="Blue (525nm)" package="5 mm [THT]"]
  Ethernet_Jack = female pin header, 8 pins [form="♀ (female)"]
  R1 = Resistor [tolerance=±5% resistance=250 package=THT]
  Ethernet_Jack2 = female pin header, 8 pins [form="♀ (female)"]
  U1 = 941H-2C-5D [package=relay-5v]
  R2 = Resistor [tolerance=±5% resistance=270 package=THT]
  U2 = 941H-2C-5D [package=relay-5v]
  U3 = 941H-2C-5D [package=relay-5v]

nets:
  GND: Ch3_LED.cathode, Ch1_Switch.L2, Ch2_Switch.L2, Ch3_Switch.L2, Solo_Switch.COM, Ch2_LED.cathode, Ch1_LED.anode, Amp_Switch.2, Amp_Switch.5, Ethernet_Jack.pin8, Ethernet_Jack2.pin8, U2.1, U3.1
  N1: Ch3_LED.anode, Ch1_LED.cathode, U1.9
  N2: Solo_LED.cathode, Solo_Switch.L1
  N3: Solo_LED.anode, Amp1_LED.anode, Amp2_LED.anode, U1.6, R2.Pin_0
  N4: Ch1_Switch.COM, Ethernet_Jack.pin7
  N5: Ch2_Switch.COM, Ethernet_Jack.pin6
  N6: Ch3_Switch.COM, Ethernet_Jack.pin5
  N7: Solo_Switch.L2, Ethernet_Jack.pin4
  N8: Amp1_LED.cathode, Amp_Switch.1
  N9: Ch2_LED.anode, U1.11
  N10: Amp_Switch.3, Amp2_LED.cathode
  N11: Amp_Switch.6, Ethernet_Jack.pin3
  N12: Ethernet_Jack.pin1, R2.Pin_1
  N13: Ethernet_Jack.pin2, U1.1
  N14: R1.Pin_0, U1.8
  N15: R1.Pin_1, U1.16
  9V: Ethernet_Jack2.pin1, U2.9
  N16: Ethernet_Jack2.pin2, U3.11
  N17: U1.4, U1.13
  -9V: U2.11
  N18: U2.13, U3.13

custom parts:
  941H-2C-5D: DPDT Relay - 2 Form C
